# Fritzing sketch Trash-can-circuit-schematic (saved by Fritzing 0.9.3b)
breadboards: 1

parts:
  Arduino_Uno = Arduino Uno (Rev3)
  Grove_Ultrasonic_Ranger = Grove Buzz
  ESP8266-01 = ESP8266 WiFi Module [part_number=ESP8266]

nets:
  N1: Arduino_Uno.D10_PWM/SS, ESP8266-01.TXD
  N2: Arduino_Uno.D11_PWM/MOSI, ESP8266-01.RXD
  N3: Arduino_Uno.D7, Grove_Ultrasonic_Ranger.SIG
  VCC: Arduino_Uno.5V, Grove_Ultrasonic_Ranger.VCC, ESP8266-01.VCC, ESP8266-01.CH_PD
  GND: Arduino_Uno.GND, Grove_Ultrasonic_Ranger.GND, ESP8266-01.GND

custom parts:
  ESP8266 WiFi Module: Generic WiFi Module based on the ESP8266 with onboard PCB antenna and UART communications
